# Fritzing sketch Esquema de montagem (saved by Fritzing 0.9.3b)
circuit board: 13.1562cm x 6.58988cm
breadboards: 1

parts:
  Componente2 = Soil Moisture Sensor
  KY-1 = Keyes Relay [package=THT]
  L1 = Solenoid
  DS2 = DS18B20 1-Wire Temperature Sensor [part_number=DS18B20]
  R3 = Resistor [tolerance=±5% resistance=220 package="2512 [SMD]"]
  U2 = NodeMCU V1.0

nets:
  N1: Componente2.SIG, U2.A0
  GND: Componente2.GND, KY-1.ground, DS2.GND, U2.GND
  VCC: Componente2.VCC, KY-1.power, DS2.VDD, R3.Pin_0, U2.3V3
  N2: KY-1.signal, U2.D6
  N3: KY-1.C, L1.pin2
  N4: DS2.DQ, R3.Pin_1, U2.D1

notes:
  Sensor de fluxo
  RED = 5v
  Yellow = Signal
  Black = Ground
  +12V
  -12V
  10k
  RELAY
  Válvula Solenóide
  Sensor de humidade do solo
  Módulo LDR
  VCC = 3.3v ou 5v
  GND = Negativo
  DO = Saida digital
  Sensor de Temperatura DS18B20

custom parts:
  Keyes Relay: The Keyes 5V relay module is suitable for SCM development, home appliance control. It uses a 5V~12V TIL control signal which can control DC / AC signal.
  NodeMCU V1.0: ESP8266 based NodeMCU
