# Fritzing sketch diagram (saved by Fritzing 0.9.3b)
breadboards: 1

parts:
  U4 = NodeMCU V1.0
  Componente4 = Soil Moisture Sensor
  KY-3 = Keyes Relay [package=THT]
  DS4 = DS18B20 1-Wire Temperature Sensor [part_number=DS18B20]
  R5 = Resistor [tolerance=±5% resistance=220 package="2512 [SMD]"]
  VALVE2 = Plastic Solenoid Valve
  YF-S201_Flow_Meter2 = YF-S201 Water Flow Meter

nets:
  N1: U4.D1, DS4.DQ, R5.Pin_1
  N2: U4.D2, YF-S201_Flow_Meter2.SIG
  GND: U4.GND, Componente4.GND, KY-3.ground, DS4.GND, YF-S201_Flow_Meter2.GND
  N3: U4.D6, KY-3.signal
  VCC: U4.3V3, Componente4.VCC, KY-3.power, DS4.VDD, R5.Pin_0, YF-S201_Flow_Meter2.VCC
  N4: U4.A0, Componente4.SIG
  N5: KY-3.NC, VALVE2.no_name_yet

notes:
  12v
  GND

custom parts:
  NodeMCU V1.0: ESP8266 based NodeMCU
  Keyes Relay: The Keyes 5V relay module is suitable for SCM development, home appliance control. It uses a 5V~12V TIL control signal which can control DC / AC signal.
  YF-S201 Water Flow Meter: The YF-S201 Flow Meter. The input voltage is 5V to 24V (DC).
